# Fritzing sketch grow_light (saved by Fritzing 0.9.3b)
breadboards: 1

parts:
  U1 = 2-Channel 5v Relay Shield [package=relay-2ch5v10a]
  Part1 = Arduino Uno (Rev3) - ICSP
  LED1 = smd LED [color="Red (633nm)" package="0603 [SMD]"]
  Power_plug1 = Power plug

nets:
  VCC: U1.VCC, Part1.5V
  N1: U1.IN1, Part1.D7
  N2: U1.K1-In, Power_plug1.GND
  N3: U1.K1-On, LED1.anode

custom parts:
  2-Channel 5v Relay Shield: 2 Channel 5v Relay Shield w. 2x SPD-06VDC-SD-C
