# Fritzing sketch ultrasonic fogger (saved by Fritzing 0.9.3b)
breadboards: 1

parts:
  Part1 = Arduino Uno (Rev3) - ICSP
  LED1 = smd LED [color="Red (633nm)" package="0603 [SMD]"]
  Power_plug1 = Power plug
  U1 = 2-Channel 5v Relay Shield [package=relay-2ch5v10a]
  J1 = Piezo Speaker

nets:
  N1: Part1.D6_PWM, U1.IN2
  N2: Part1.D7, U1.IN1
  5V: Part1.5V, U1.VCC
  N3: LED1.anode, U1.K1-On
  N4: Power_plug1.GND, U1.K1-In
  N5: U1.K2-In, J1.pin1
  N6: U1.K2-On, J1.pin2

custom parts:
  2-Channel 5v Relay Shield: 2 Channel 5v Relay Shield w. 2x SPD-06VDC-SD-C
